// Logisim project CPU.circ as structural Verilog: 1 circuit, main circuit main
module main (
  output [7:0] out_1,
  output [2:0] out_2,
  output [7:0] out_3
);

  wire alu_1_p5, alu_1_p7, clock_1_out, controlled_buffer_9_out, controlled_buffer_12_out, cu_1_acc_en,
       cu_1_acc_set, cu_1_flag_set, cu_1_inst_set, cu_1_pc_clk, cu_1_pc_h, cu_1_pc_l, cu_1_r0_en,
       cu_1_r0_set, cu_1_r1_en, cu_1_r1_set, cu_1_r2_en, cu_1_r2_set, cu_1_r3_en, cu_1_r3_set, cu_1_r4_en,
       cu_1_r4_set, cu_1_r5_en, cu_1_r5_set, cu_1_r6_en, cu_1_r6_set, cu_1_r7_en, cu_1_r7_set, cu_1_ram_clk,
       cu_1_ram_en, cu_1_ram_h, cu_1_ram_l, cu_1_ram_set, cu_1_rom_en, pc_1_increment_next,
       RAM_L_increment_next, undriven;
  wire [2:0] alu_1_p8;
  wire [7:0] ACC_q, alu_1_p1, controlled_buffer_1_out, Flags_q, INST_q, MUL_In_q, pc_1_pc_out, pc_2_pc_out,
       R0_A_q, R2_q, R3_q, R4_q, R5_q, R6_q, R7_q, ram_1_dout, RAM_H_pc_out, RAM_L_pc_out, rom_1_data;

  Register #(.trigger("high")) R0_A (
    .D(controlled_buffer_1_out), .en(cu_1_r0_set), .clk(1'b1), .Q(R0_A_q));  // open: clr
  Register #(.trigger("high")) MUL_In (
    .D(controlled_buffer_1_out), .en(undriven), .clk(1'b1), .Q(MUL_In_q));  // open: clr
  Register #(.trigger("high")) ACC (.D(out_3), .en(cu_1_acc_set), .clk(1'b1), .Q(ACC_q));  // open: clr
  assign controlled_buffer_1_out = cu_1_r0_en ? R0_A_q : 8'bz;  // Controlled_Buffer controlled_buffer_1
  // ALU alu_1: pin names not known; wires that end beside it: alu_1_p1, out_3, R0_A_q, controlled_buffer_1_out, alu_1_p5, MUL_In_q, alu_1_p7, alu_1_p8, out_2
  assign controlled_buffer_1_out = cu_1_acc_en ? ACC_q : 8'bz;  // Controlled_Buffer controlled_buffer_2
  Register #(.trigger("high")) R1_B (
    .D(controlled_buffer_1_out), .en(cu_1_r1_set), .clk(1'b1), .Q(alu_1_p1));  // open: clr
  Register #(.trigger("high")) R2 (.D(controlled_buffer_1_out), .en(cu_1_r2_set), .clk(1'b1), .Q(R2_q));  // open: clr
  assign controlled_buffer_1_out = cu_1_r1_en ? alu_1_p1 : 8'bz;  // Controlled_Buffer controlled_buffer_3
  CU cu_1 (
    .Adress_Input(controlled_buffer_1_out), .Flags(Flags_q), .Instruction(INST_q), .Clk(clock_1_out),
    .Mul_In(undriven), .Cin(alu_1_p7), .Flag_set(cu_1_flag_set), .R0_Set(cu_1_r0_set), .R1_Set(cu_1_r1_set),
    .R2_Set(cu_1_r2_set), .R3_Set(cu_1_r3_set), .R4_Set(cu_1_r4_set), .R5_Set(cu_1_r5_set),
    .R6_Set(cu_1_r6_set), .R7_Set(cu_1_r7_set), .R0_En(cu_1_r0_en), .R1_En(cu_1_r1_en), .R2_En(cu_1_r2_en),
    .R3_En(cu_1_r3_en), .R4_En(cu_1_r4_en), .R5_En(cu_1_r5_en), .R6_En(cu_1_r6_en), .R7_En(cu_1_r7_en),
    .Inst_Set(cu_1_inst_set), .RAM_CLK(cu_1_ram_clk), .RAM_L(cu_1_ram_l), .RAM_H(cu_1_ram_h),
    .RAM_SET(cu_1_ram_set), .RAM_EN(cu_1_ram_en), .ALU(out_2), .PC_CLK(cu_1_pc_clk), .PC_L(cu_1_pc_l),
    .PC_H(cu_1_pc_h), .Adress_Output(controlled_buffer_1_out), .ROM_En(cu_1_rom_en), .ACC_En(cu_1_acc_en),
    .ACC_Set(cu_1_acc_set), .Cout(alu_1_p5), .Shift(alu_1_p8));  // open: Ext_Reset, Halt_In, JP1, JP2, Halt
  Clock clock_1 (.out(clock_1_out));
  Register #(.trigger("high")) Flags (
    .D(controlled_buffer_1_out), .en(cu_1_flag_set), .clk(1'b1), .Q(Flags_q));  // open: clr
  assign controlled_buffer_1_out = cu_1_r2_en ? R2_q : 8'bz;  // Controlled_Buffer controlled_buffer_4
  Register #(.trigger("high")) R3 (.D(controlled_buffer_1_out), .en(cu_1_r3_set), .clk(1'b1), .Q(R3_q));  // open: clr
  Register #(.trigger("high")) INST (
    .D(controlled_buffer_1_out), .en(cu_1_inst_set), .clk(1'b1), .Q(INST_q));  // open: clr
  Register #(.trigger("high")) R4 (.D(controlled_buffer_1_out), .en(cu_1_r4_set), .clk(1'b1), .Q(R4_q));  // open: clr
  assign controlled_buffer_1_out = cu_1_r3_en ? R3_q : 8'bz;  // Controlled_Buffer controlled_buffer_5
  assign controlled_buffer_1_out = cu_1_r4_en ? R4_q : 8'bz;  // Controlled_Buffer controlled_buffer_6
  Register #(.trigger("high")) R5 (.D(controlled_buffer_1_out), .en(cu_1_r5_set), .clk(1'b1), .Q(R5_q));  // open: clr
  assign controlled_buffer_1_out = cu_1_r5_en ? R5_q : 8'bz;  // Controlled_Buffer controlled_buffer_7
  Register #(.trigger("high")) R6 (.D(controlled_buffer_1_out), .en(cu_1_r6_set), .clk(1'b1), .Q(R6_q));  // open: clr
  Register #(.trigger("high")) R7 (.D(controlled_buffer_1_out), .en(cu_1_r7_set), .clk(1'b1), .Q(R7_q));  // open: clr
  assign controlled_buffer_1_out = cu_1_r6_en ? R6_q : 8'bz;  // Controlled_Buffer controlled_buffer_8
  assign controlled_buffer_9_out = cu_1_pc_clk ? cu_1_pc_clk : 1'bz;  // Controlled_Buffer controlled_buffer_9
  assign controlled_buffer_9_out = cu_1_pc_l ? cu_1_pc_l : 1'bz;  // Controlled_Buffer controlled_buffer_10
  assign controlled_buffer_1_out = cu_1_r7_en ? R7_q : 8'bz;  // Controlled_Buffer controlled_buffer_11
  assign controlled_buffer_12_out = controlled_buffer_9_out ? controlled_buffer_9_out : 1'bz;  // Controlled_Buffer controlled_buffer_12
  assign controlled_buffer_12_out = cu_1_pc_h ? cu_1_pc_h : 1'bz;  // Controlled_Buffer controlled_buffer_13
  PC RAM_L (
    .CLK(cu_1_ram_clk), .Jump_Pos(controlled_buffer_1_out), .Jump_Signal(cu_1_ram_l), .PC_OUT(RAM_L_pc_out),
    .Increment_Next(RAM_L_increment_next));  // open: EN
  PC RAM_H (
    .CLK(cu_1_ram_clk), .Jump_Pos(controlled_buffer_1_out), .Jump_Signal(cu_1_ram_h),
    .EN(RAM_L_increment_next), .PC_OUT(RAM_H_pc_out));  // open: Increment_Next
  PC pc_1 (
    .CLK(controlled_buffer_9_out), .Jump_Pos(controlled_buffer_1_out), .Jump_Signal(cu_1_pc_l), .EN(1'b1),
    .PC_OUT(pc_1_pc_out), .Increment_Next(pc_1_increment_next));
  PC pc_2 (
    .CLK(controlled_buffer_12_out), .Jump_Pos(controlled_buffer_1_out), .Jump_Signal(cu_1_pc_h),
    .EN(pc_1_increment_next), .PC_OUT(pc_2_pc_out));  // open: Increment_Next
  Controlled_Buffer #(.width(8)) controlled_buffer_14 (.in(ram_1_dout));  // open: out, en
  RAM #(.addrWidth(16)) ram_1 (
    .addr({RAM_H_pc_out, RAM_L_pc_out}), .we(cu_1_ram_set), .oe(cu_1_ram_en), .clk(cu_1_ram_en),
    .din(controlled_buffer_1_out), .dout(ram_1_dout));
  ROM #(.addrWidth(16)) rom_1 (.addr({pc_2_pc_out, pc_1_pc_out}), .data(rom_1_data));
  assign controlled_buffer_1_out = cu_1_rom_en ? rom_1_data : 8'bz;  // Controlled_Buffer controlled_buffer_15

  // Notes on the sheet:
  //   contents of rom_1 (hex, n*v repeats v):
  //   50 7*e 0 0 58 85 85 86 84 44 7 44 7 44 7 44 7 44 7 44 7 44 7 44 7 44 7 44 7 44 7 44 7 44 7 44 7 44 7
  //   44 7 44 7 44 7 44 7 44 7 44 7 44 7 44 7 44 7 44 7 44 7 44 7 44 7 44 7 44 7 44 7 44 7 44 7 44 7 44 7
  //   44 7 44 7 44 7 44 7 44 7 44 7 44 7 44 7 44 7 44 7 44 7 44 7 44 7 44 7 44 7 44 7 44 7 44 7 44 7 44 7
  //   44 7 44 7 44 7 44 7 44 7 44 7 44 7 44 7 44 7 44 7 44 7 44 7 44 7 44 7 44 7 44 7 44 7 44 7 44 7 44 7
  //   44 7 44 7 44 7 44 7 44 7 44 7 44 7 44 7 44 7 44 7 44 7 44 7 44 7 44 7 44 7 44 7 44 7 44 7 44 7 44 7
  //   44 7 44 7 44 7 44 7 44 7 44 7 44 7 44 7 44 7 44 7 44 7 44 7 44 7 44 7 44 7 44 7 44 7 44
endmodule
